# Fritzing sketch Irrigação Automática Jardim (saved by Fritzing 0.9.2b)
circuit board: 7.2cm x 6.2cm
breadboards: 3

parts:
  D1 = Rectifier Diode [part_number=1N4001 package="300 mil [THT]"]
  Q1 = NPN-Transistor [part_number=BC547 package="TO92 [THT]"]
  D2 = Rectifier Diode [part_number=1N4001 package="300 mil [THT]"]
  D3 = Rectifier Diode [part_number=1N4001 package="300 mil [THT]"]
  Q2 = NPN-Transistor [part_number=BC547 package="TO92 [THT]"]
  Q3 = NPN-Transistor [part_number=BC547 package="TO92 [THT]"]
  R5 = Resistor [tolerance=±5% resistance=2.2k package=THT]
  R6 = Resistor [tolerance=±5% resistance=10k package=THT]
  R3 = Resistor [tolerance=±5% resistance=2.2k package=THT]
  R4 = Resistor [tolerance=±5% resistance=10k package=THT]
  R1 = Resistor [tolerance=±5% resistance=2.2k package=THT]
  R2 = Resistor [tolerance=±2% resistance=10k package=THT]
  OLED = female pin header, 4 pins [form="♀ (female)"]
  Buzzer = female pin header, 2 pins [form="♀ (female)"]
  SW1 = female pin header, 2 pins [form="♀ (female)"]
  SW2 = female pin header, 2 pins [form="♀ (female)"]
  SW3 = female pin header, 2 pins [form="♀ (female)"]
  Relê_1 = songle relay
  Relê_2 = songle relay
  Relê_3 = songle relay
  Flow = female pin header, 3 pins [form="♀ (female)"]
  ESP-12E = NodeMCU V1.0
  Fonte_5V = HLK-PM01
  127V = female pin header, 2 pins [form="♀ (female)"]
  ON/OFF = female alternating pin header, 2 pins [form="♀ (female)"]
  CH3 = female pin header, 2 pins [form="♀ (female)"]
  CH2 = female pin header, 2 pins [form="♀ (female)"]
  CH1 = female pin header, 2 pins [form="♀ (female)"]
  A0 = female pin header, 1 pin [form="♀ (female)"]
  D0 = female pin header, 1 pin [form="♀ (female)"]
  D4 = female pin header, 1 pin [form="♀ (female)"]
  SD0 = female pin header, 1 pin [form="♀ (female)"]
  GND = female pin header, 1 pin [form="♀ (female)"]
  3V3 = female pin header, 1 pin [form="♀ (female)"]
  5V = female pin header, 1 pin [form="♀ (female)"]

nets:
  VCC 5V: D1.cathode, D2.cathode, D3.cathode, Relê_1.GND, Relê_2.GND, Relê_3.GND, Flow.pin2, ESP-12E.Vin, Fonte_5V.+Vo, 5V.pin1
  N1: D1.anode, Q1.C, Relê_1.VCC
  GND: Q1.E, Q2.E, Q3.E, R6.Pin_0, R4.Pin_0, R2.Pin_0, OLED.pin1, Buzzer.pin1, SW1.pin1, SW2.pin1, SW3.pin1, Flow.pin1, ESP-12E.GND, Fonte_5V.-Vo, GND.pin1
  N2: Q1.B, R1.Pin_0
  N3: D2.anode, Q2.C, Relê_2.VCC
  N4: D3.anode, Q3.C, Relê_3.VCC
  N5: Q2.B, R3.Pin_0
  N6: Q3.B, R5.Pin_0
  Canal 3: R5.Pin_1, R6.Pin_1, ESP-12E.D8
  Canal 2: R3.Pin_1, R4.Pin_1, ESP-12E.D7
  Canal 1: R1.Pin_1, R2.Pin_1, ESP-12E.D6
  N7: OLED.pin2, ESP-12E.3V3, 3V3.pin1
  N8: OLED.pin3, ESP-12E.D5
  N9: OLED.pin4, ESP-12E.D3
  N10: Buzzer.pin2, ESP-12E.D1
  N11: SW1.pin2, ESP-12E.SD3
  N12: SW2.pin2, ESP-12E.SD2
  N13: SW3.pin2, ESP-12E.SD1
  N14: Relê_1.NO, CH1.pin1
  F AC 127V: Relê_1.COMMON, Relê_2.COMMON, Relê_3.COMMON, Fonte_5V.AC#0, ON/OFF.pin2
  N15: Relê_2.NO, CH2.pin1
  N16: Relê_3.NO, CH3.pin1
  N17: Flow.pin3, ESP-12E.D2
  N18: ESP-12E.D0, D0.pin1
  N19: ESP-12E.D4, D4.pin1
  N20: ESP-12E.SD0, SD0.pin1
  N21: ESP-12E.A0, A0.pin1
  N AC127V: Fonte_5V.AC#1, 127V.pin2, CH3.pin2, CH2.pin2, CH1.pin2
  N22: 127V.pin1, ON/OFF.pin1

notes:
  N     F
  Alcides - Jan/2019
  Automação
  Irrigação v1.0

custom parts:
  NodeMCU V1.0: ESP8266 based NodeMCU
  HLK-PM01: AC-DC 220V to 5V Step-Down Power Supply Module

// code stored in the sketch: Node_B_receiver.ino
#include <SoftwareSerial.h>

#define D7 13
#define D8 15

SoftwareSerial mySerial(D7, D8); // RX = D7, TX  = D8


void setup() {
  Serial.begin(9600); //Start Serial
  mySerial.begin(9600); //Start mySerial
  pinMode(D7,INPUT); //d7 is RX, receiver, so define it as input
  pinMode(D8,OUTPUT); //d8 is TX, transmitter, so define it as output
} // end of setup

void loop() {
  char receivedLetter = '?'; // if empty show question mark
  
  if (mySerial.available() > 0) { //Check if serial is avaliable, if this check is not done you will read 'ÿ'
    receivedLetter = mySerial.read(); //read the char received. This function returns -1 if there is nothing to read.
    Serial.print("LETRA ");Serial.print(receivedLetter); Serial.println(" RECEBIDA"); // Write on serial monitor which letter was received. 
  }
  
} //end of loop
